// Logisim project LedMatrix.circ as structural Verilog: 1 circuit, main circuit main
module main (
  input  [6:0] _1,
  input  [6:0] _2,
  input  [6:0] _3,
  input  [6:0] _4,
  input  [6:0] _5
);

  wire [6:0] nand_1_out, not_1_out, not_2_out, xnor_1_out, xor_1_out;

  assign not_1_out = ~_5;  // NOT_Gate not_1, 7 bits wide
  assign not_2_out = ~_1;  // NOT_Gate not_2, 7 bits wide
  NotExactlyOne xnor_1[6:0] (.out(xnor_1_out), .in0(_4), .in1(_4), .in2(not_1_out));
  DotMatrix dotmatrix_1 (.col0(not_2_out), .col1(xor_1_out), .col2(nand_1_out), .col3(_4), .col4(xnor_1_out));
  ExactlyOne xor_1[6:0] (.out(xor_1_out), .in0(not_2_out), .in1(_2), .in2(_2));
  assign nand_1_out = ~(_2 & _3);  // NAND_Gate nand_1, 7 bits wide
endmodule
